# Fritzing sketch homersekleSzabalyzoRajz (saved by Fritzing 0.9.9b)
breadboards: 1

parts:
  Mod1 = Raspberry Pi 4B
  DS2 = DS18B20 1-Wire Temperature Sensor [part_number=DS18B20]
  R1 = Resistor [tolerance=±5% resistance=4.7k package="1206 [SMD]"]
  LED1 = RGB LED (com. anode, rbg) [package="5 mm [THT]"]
  R2 = Resistor [tolerance=±5% resistance=3.3k package="1206 [SMD]"]
  R3 = Resistor [tolerance=±5% resistance=3.3k package="1206 [SMD]"]
  R4 = Resistor [tolerance=±5% resistance=3.3k package="1206 [SMD]"]
  7SEG1 = 7-Segment LED I2C Backpack (blue)  # not connected
  U1 = 2-Channel 5v Relay Shield [package=relay-2ch5v10a]  # not connected

nets:
  3V3: Mod1.3V3, DS2.VDD, R1.Pin_0
  GND: Mod1.GND, Mod1.GPIO27, DS2.GND, LED1.common_anode, R3.Pin_0
  N1: Mod1.GPIO4, DS2.DQ, R1.Pin_1
  N2: Mod1.GPIO17, R2.Pin_0
  N3: Mod1.GPIO22, R4.Pin_0
  N4: LED1.red_cathode, R2.Pin_1
  N5: LED1.blue_cathode, R3.Pin_1
  N6: LED1.green_cathode, R4.Pin_1

custom parts:
  7-Segment LED I2C Backpack (blue): 4-digit, 7-segment LED Display with I2C Control
  2-Channel 5v Relay Shield: 2 Channel 5v Relay Shield w. 2x SPD-06VDC-SD-C
